# Fritzing sketch 3-Axis Gyroscope & 3-Axis Accelerometer (saved by Fritzing 0.9.5d)
breadboards: 1

parts:
  Part1 = Maker Uno (Arduino Uno Compatible)
  GY1 = GY-521 (MPU-6050) [form="♀ (female)" package=THT]

nets:
  N1: Part1.A4/SDA, GY1.pin4
  N2: Part1.A5/SCL, GY1.pin3
  N3: Part1.D2, GY1.pin8
  N4: Part1.5V, GY1.pin1
  N5: Part1.GND, GY1.pin2

custom parts:
  Maker Uno (Arduino Uno Compatible): Maker Uno, an Arduino UNO compatible board designed and developed specially for students to learn coding and microcontroller. We named it Maker UNO to encourage everyone to be a maker by getting started with this amazing board. Oh! BTW, it is PURPLE color.
  GY-521 (MPU-6050): Placa GY-521 basada en conjunto de acelerómetro+giroscopios MPU-6050
