# Fritzing sketch Active Buzzer (saved by Fritzing 0.9.5d)
breadboards: 1

parts:
  Part1 = Maker Uno (Arduino Uno Compatible)
  Part2 = KY-012 Active Buzzer Module [package="Breakout board"]

nets:
  N1: Part1.A0, Part2.S
  N2: Part1.GND, Part2.-

custom parts:
  Maker Uno (Arduino Uno Compatible): Maker Uno, an Arduino UNO compatible board designed and developed specially for students to learn coding and microcontroller. We named it Maker UNO to encourage everyone to be a maker by getting started with this amazing board. Oh! BTW, it is PURPLE color.
  KY-012 Active Buzzer Module: Active Piezoelectric Buzzer Module Keyes KY-012, it produces single-tone sound when signal is high.
