# Fritzing sketch WiFi Ethernet Module (saved by Fritzing 0.9.5d)
breadboards: 1

parts:
  Part1 = Maker Uno (Arduino Uno Compatible)
  U1 = ESP8266 WiFi Module [part_number=ESP8266]

nets:
  N1: Part1.D0/RX, U1.RXD
  N2: Part1.D1/TX, U1.TXD
  N3: Part1.3V3, U1.CH_PD
  GND: Part1.GND, U1.GND

custom parts:
  Maker Uno (Arduino Uno Compatible): Maker Uno, an Arduino UNO compatible board designed and developed specially for students to learn coding and microcontroller. We named it Maker UNO to encourage everyone to be a maker by getting started with this amazing board. Oh! BTW, it is PURPLE color.
  ESP8266 WiFi Module: Generic WiFi Module based on the ESP8266 with onboard PCB antenna and UART communications
